# Fritzing sketch scheme (saved by Fritzing 0.9.4)
breadboards: 1

parts:
  Компонент1 = Arduino Uno (Rev3)
  M1 = Stepper Motor - Unipolar
  U1 = POT [package=pot_alpha_rv16af-20]
  S1 = Pushbutton [package="[SMD]"]
  S2 = Pushbutton [package="[SMD]"]
  R1 = Resistor [tolerance=±5% resistance=220 package="2512 [SMD]"]
  R2 = Resistor [tolerance=±5% resistance=220 package="2512 [SMD]"]
  DI1 = 7-Segment LED Display [package=THT]

nets:
  N1: Компонент1.A1, M1.D
  N2: Компонент1.A3, M1.C
  N3: Компонент1.A4/SDA, M1.A
  N4: Компонент1.A5/SCL, U1.S
  N5: Компонент1.D8, DI1.cathodeA
  N6: Компонент1.D12/MISO, S1.Pin_1, S1.Pin_2, R1.Pin_0
  N7: Компонент1.D13/SCK, S2.Pin_1, S2.Pin_2, R2.Pin_0
  N8: Компонент1.D2, DI1.cathodeG
  N9: Компонент1.D3_PWM, DI1.commAnode#7, DI1.cathodeF
  N10: Компонент1.D4, DI1.cathodeE
  N11: Компонент1.D5_PWM, DI1.cathodeD
  N12: Компонент1.D6_PWM, DI1.cathodeDP
  N13: Компонент1.D7, DI1.cathodeB
  N14: Компонент1.5V, M1.COMMON_1, U1.A, S1.Pin_3, S1.Pin_4, S2.Pin_3, S2.Pin_4
  N15: Компонент1.GND, M1.COMMON_2, U1.E, R1.Pin_1, R2.Pin_1, DI1.commAnode#2, DI1.cathodeC
